# Fritzing sketch ElectroMagnet (saved by Fritzing 1.0.4)
circuit board: 2.52663cm x 2.53467cm
breadboards: 1

parts:
  F1 = FUSE [package=fuse_5mm]
  12v/24v = longpad pin header, 3 pins [form="long pad"]
  LED = longpad pin header, 2 pins [form="long pad"]
  S1 = Toggle Switch [package=THT]
  LED1 = LED - 5mm [color="Red (633nm)" current=0.030A package="5 mm [THT]"]
  EM = Solenoid
  Bat = molex pin header, 2 pins [form=molex]
  EM_Conn = molex pin header, 2 pins [form=molex]
  Switch = molex pin header, 2 pins [form=molex]
  BC = molex pin header, 4 pins [form=molex]
  Part1 = VERTER 5V USB Buck-Boost

nets:
  N1: F1.1, S1.COM, Switch.pin2
  N2: F1.2, Bat.pin2
  N3: 12v/24v.pin1, EM.pin2, EM_Conn.pin1, BC.pin4, Part1.5.0V
  N4: 12v/24v.pin2, LED.pin2, S1.L2, LED1.anode, Switch.pin1
  N5: 12v/24v.pin3, BC.pin2, Part1.VIN
  N6: LED.pin1, LED1.cathode, EM.pin1, Bat.pin1, EM_Conn.pin2, BC.pin1, BC.pin3, Part1.GND

custom parts:
  VERTER 5V USB Buck-Boost: VERTER can take battery voltages from 3-12VDC and output a nice 5V DC, which makes it a perfect universal power supply for your portable project! Where Verter really shines is when you have a battery or power range that can fluctuate a lot, or you don't know what you'll end up using.
