# Fritzing sketch ledModule (saved by Fritzing 1.0.4)
circuit board: 1.5cm x 2.5cm
breadboards: 1

parts:
  LED3 = LED - 5mm [color="Red (633nm)" current=0.030A package="5 mm [THT]"]
  LED4 = LED - 5mm [color="Red (633nm)" current=0.030A package="5 mm [THT]"]
  R1 = Resistor [tolerance=±5% power=0.25W resistance=300 package=THT]
  PWR = longpad pin header, 2 pins [form="long pad"]
  LED5 = LED - 5mm [color="Red (633nm)" current=0.030A package="5 mm [THT]"]
  LED6 = LED - 5mm [color="Red (633nm)" current=0.030A package="5 mm [THT]"]
  R2 = Resistor [tolerance=±5% power=0.25W resistance=300 package=THT]
  L1 = longpad pin header, 2 pins [form="long pad"]
  L2 = longpad pin header, 2 pins [form="long pad"]

nets:
  N1: LED3.cathode, LED4.anode
  N2: LED3.anode, PWR.pin2, LED5.anode, L1.pin2, L2.pin2
  N3: LED4.cathode, R1.Pin_1, L1.pin1
  N4: R1.Pin_0, PWR.pin1, R2.Pin_0
  N5: LED5.cathode, LED6.anode
  N6: LED6.cathode, R2.Pin_1, L2.pin1
